# Fritzing sketch MPU6050_Acelero_Gyro (saved by Fritzing 0.9.9b)
breadboards: 1

parts:
  WeMos_D1_Mini1 = WeMos D1 Mini  # not connected
  GY1 = MPU-6050 Board GY-521 [form="♀ (female)" package=THT]
  OLED_I2C1 = OLED 128x64 I2C Monochrome Display

nets:
  N1: GY1.pin1, OLED_I2C1.VDD
  N2: GY1.pin2, OLED_I2C1.GND
  N3: GY1.pin3, OLED_I2C1.SCK
  N4: GY1.pin4, OLED_I2C1.SDA

custom parts:
  MPU-6050 Board GY-521: Acelerometro y Giroscopio MPU-6050 Board GY-521
